# Fritzing sketch Circuit capteur (saved by Fritzing 0.9.3b)
breadboards: 1

parts:
  Composant1 = Arduino Uno (Rev3)
  U1 = LM124-324 Quad Opamp [package="DIP (Dual Inline)"]
  Q1 = TRANSISTOR_NPN [package=to-92]
  C1 = Capacitor Polarized [package=panasonic_e]
  R2 = Resistor [tolerance=±5% resistance=470k package=THT]
  C2 = Capacitor [package=0402-cap]
  R3 = Resistor [tolerance=±5% resistance=1.8k package="1206 [SMD]"]
  C3 = Capacitor [package=0402-cap]
  R4 = Resistor [tolerance=±5% resistance=8.2k package="1206 [SMD]"]
  R5 = Resistor [tolerance=±5% resistance=68k package="1206 [SMD]"]
  C4 = Capacitor Polarized [package=panasonic_e]
  R6 = Resistor [tolerance=±5% resistance=68k package="1206 [SMD]"]
  R7 = Resistor [tolerance=±5% resistance=39k package="1206 [SMD]"]
  R8 = Resistor [tolerance=±5% resistance=220k package="1206 [SMD]"]
  LED2 = smd LED [color="Red (633nm)" package="1206 [SMD]"]
  Q2 = LTR-301 [package=ltr-301]

nets:
  N1: Composant1.A0, Q1.E
  N2: Composant1.GND, R5.Pin_0
  N3: Composant1.5V, Q1.C, R7.Pin_1
  N4: U1.1OUT, C1.+, C3.1
  N5: U1.1IN-, C3.2, R4.Pin_1
  N6: U1.1IN+, C4.-, R6.Pin_1
  N7: U1.4IN-, R2.Pin_0, C2.2
  N8: U1.4OUT, R2.Pin_1, C2.1, R3.Pin_0
  N9: C1.-, R5.Pin_1
  N10: C4.+, R7.Pin_0
  N11: R6.Pin_0, LED2.cathode, Q2.E
  N12: R8.Pin_0, LED2.anode
